// Logisim project PixelToXY.circ as structural Verilog: 1 circuit, main circuit main
module main (
  input  [7:0] Character,
  input  [2:0] FrontColor,
  input  [2:0] BackColor,
  input  [9:0] HSync,
  input  [9:0] VSync,
  input  Ready,
  input  [7:0] RomData,
  output [6:0] XPosition,
  output [5:0] YPosition,
  output Red,
  output Green,
  output Blue,
  output [11:0] RomAddress
);

  wire multiplexer_2_out;

  Multiplexer #(.width(3), .disabled(0)) multiplexer_1 (
    .in0(BackColor), .in1(FrontColor), .out({Blue, Green, Red}), .sel(multiplexer_2_out), .en(Ready));
  Multiplexer #(.select(3), .disabled(0)) multiplexer_2 (
    .in0(RomData[0]), .in1(RomData[1]), .in2(RomData[2]), .in3(RomData[3]), .in4(RomData[4]),
    .in5(RomData[5]), .in6(RomData[6]), .in7(RomData[7]), .out(multiplexer_2_out), .sel(HSync[2:0]),
    .en(Ready));

  assign RomAddress = {Character, VSync[3:0]};
  assign XPosition = HSync[9:3];
  assign YPosition = VSync[9:4];
endmodule
