// Logisim project VGATiming.circ as structural Verilog: 1 circuit, main circuit main
module main (
  input  Red,
  input  Green,
  input  Blue,
  output [9:0] H_Pixel,
  output [9:0] V_Pixel,
  output HSync,
  output VSync,
  output Ready,
  output Red_2,
  output Green_2,
  output Blue_2
);

  wire clock_1_out, comparator_1_lt, comparator_2_gt, comparator_3_gt, comparator_4_gt, comparator_5_gt,
       comparator_6_lt, d_ff_1_q, H_Counter_carry;
  wire [9:0] H_Counter_q, subtractor_1_out, subtractor_2_out, V_Counter_q;

  Clock clock_1 (.out(clock_1_out));
  and and_1 (HSync, clock_1_out, comparator_2_gt);
  and and_2 (VSync, clock_1_out, d_ff_1_q, comparator_4_gt);
  and and_3 (Red_2, clock_1_out, Ready, Red);
  and and_4 (Green_2, clock_1_out, Ready, Green);
  and and_5 (Blue_2, clock_1_out, Ready, Blue);
  Comparator #(.width(10), .mode("unsigned")) comparator_1 (
    .a(H_Counter_q), .b(10'h310), .lt(comparator_1_lt));  // open: gt, eq
  Counter #(.width(10), .max('h320)) H_Counter (
    .count(1'b1), .Q(H_Counter_q), .carry(H_Counter_carry), .clk(clock_1_out));  // open: load, D, clr
  D_Flip_Flop d_ff_1 (.clk(clock_1_out), .D(H_Counter_carry), .Q(d_ff_1_q), .en(1'b1));  // open: Qn, preset, reset
  Comparator #(.width(10), .mode("unsigned")) comparator_2 (
    .a(H_Counter_q), .b(10'h1f), .gt(comparator_2_gt));  // open: eq, lt
  Comparator #(.width(10), .mode("unsigned")) comparator_3 (
    .a(H_Counter_q), .b(10'h8f), .gt(comparator_3_gt));  // open: eq, lt
  and and_6 (Ready, comparator_1_lt, comparator_3_gt, comparator_5_gt, comparator_6_lt);
  Counter #(.width(10), .max('h209)) V_Counter (
    .count(H_Counter_carry), .Q(V_Counter_q), .clk(clock_1_out));  // open: load, D, carry, clr
  Comparator #(.width(10), .mode("unsigned")) comparator_4 (
    .a(V_Counter_q), .b(10'h2), .gt(comparator_4_gt));  // open: eq, lt
  Comparator #(.width(10), .mode("unsigned")) comparator_5 (
    .a(V_Counter_q), .b(10'h26), .gt(comparator_5_gt));  // open: eq, lt
  Comparator #(.width(10), .mode("unsigned")) comparator_6 (
    .a(V_Counter_q), .b(10'h207), .lt(comparator_6_lt));  // open: gt, eq
  Subtractor #(.width(10)) subtractor_1 (
    .a(H_Counter_q), .b(10'h8f), .out(subtractor_1_out), .bin(1'b1));  // open: bout
  Subtractor #(.width(10)) subtractor_2 (
    .a(V_Counter_q), .b(10'h26), .out(subtractor_2_out), .bin(1'b1));  // open: bout
  assign H_Pixel = subtractor_1_out & {10{Ready}};  // AND_Gate and_7, 10 bits wide
  assign V_Pixel = subtractor_2_out & {10{Ready}};  // AND_Gate and_8, 10 bits wide
endmodule
