// Logisim project gpu_test.circ as structural Verilog: 3 circuits, main circuit main
module main (
);

  wire main_1_ready, main_2_blue, main_2_green, main_2_red;
  wire [3:0] main_2_romaddress, main_2_romaddress_2, main_2_romaddress_3;
  wire [7:0] demultiplexer_1_out0, demultiplexer_1_out1, demultiplexer_1_out2, demultiplexer_1_out3,
       demultiplexer_1_out4, demultiplexer_1_out5, demultiplexer_1_out6, demultiplexer_1_out7,
       demultiplexer_1_out8, demultiplexer_1_out9, demultiplexer_1_out10, demultiplexer_1_out11,
       demultiplexer_1_out12, demultiplexer_1_out13, demultiplexer_1_out14, demultiplexer_1_out15, rom_1_data;
  wire [9:0] main_1_h_pixel, main_1_v_pixel;

  Demultiplexer #(.select(4), .width(8), .disabled(0)) demultiplexer_1 (
    .out0(demultiplexer_1_out0), .out1(demultiplexer_1_out1), .out2(demultiplexer_1_out2),
    .out3(demultiplexer_1_out3), .out4(demultiplexer_1_out4), .out5(demultiplexer_1_out5),
    .out6(demultiplexer_1_out6), .out7(demultiplexer_1_out7), .out8(demultiplexer_1_out8),
    .out9(demultiplexer_1_out9), .out10(demultiplexer_1_out10), .out11(demultiplexer_1_out11),
    .out12(demultiplexer_1_out12), .out13(demultiplexer_1_out13), .out14(demultiplexer_1_out14),
    .out15(demultiplexer_1_out15), .in(rom_1_data), .sel(main_2_romaddress), .en(main_1_ready));
  DotMatrix #(.inputtype("row"), .matrixcols(8), .matrixrows(16), .persist(20000), .dotshape("circle")) dotmatrix_1 (
    .row0(demultiplexer_1_out0), .row1(demultiplexer_1_out1), .row2(demultiplexer_1_out2),
    .row3(demultiplexer_1_out3), .row4(demultiplexer_1_out4), .row5(demultiplexer_1_out5),
    .row6(demultiplexer_1_out6), .row7(demultiplexer_1_out7), .row8(demultiplexer_1_out8),
    .row9(demultiplexer_1_out9), .row10(demultiplexer_1_out10), .row11(demultiplexer_1_out11),
    .row12(demultiplexer_1_out12), .row13(demultiplexer_1_out13), .row14(demultiplexer_1_out14),
    .row15(demultiplexer_1_out15));
  VGATiming_main main_1 (
    .H_Pixel(main_1_h_pixel), .V_Pixel(main_1_v_pixel), .Ready(main_1_ready), .Red(main_2_red),
    .Green(main_2_green), .Blue(main_2_blue));  // open: HSync, VSync, Red_2, Green_2, Blue_2
  PixelToXY_main main_2 (
    .HSync(main_1_h_pixel), .VSync(main_1_v_pixel), .Ready(main_1_ready), .Red(main_2_red),
    .Green(main_2_green), .Blue(main_2_blue), .FrontColor(3'b111), .BackColor(3'b000),
    .RomAddress({main_2_romaddress_3, main_2_romaddress_2, main_2_romaddress}), .RomData(rom_1_data));  // open: XPosition, YPosition, Character
  ROM #(.addrWidth(4)) rom_1 (.addr(main_2_romaddress), .data(rom_1_data), .sel(1'b1));

  // Notes on the sheet:
  //   contents of rom_1 (hex, n*v repeats v):
  //   0 0 7e 81 a5 81 81 81 bd 99 81 81 7e
endmodule

module decoder (
  input  in_1,
  input  [2:0] in_2,
  input  [3:0] in_3,
  output [7:0] out_4,
  output [15:0] out_5
);

  Decoder #(.select(3), .disabled(0)) decoder_1 (
    .out0(out_4[0]), .out1(out_4[1]), .out2(out_4[2]), .out3(out_4[3]), .out4(out_4[4]), .out5(out_4[5]),
    .out6(out_4[6]), .out7(out_4[7]), .sel(in_2), .en(in_1));
  Decoder #(.select(4), .disabled(0)) decoder_2 (
    .out0(out_5[0]), .out1(out_5[1]), .out2(out_5[2]), .out3(out_5[3]), .out4(out_5[4]), .out5(out_5[5]),
    .out6(out_5[6]), .out7(out_5[7]), .out8(out_5[8]), .out9(out_5[9]), .out10(out_5[10]), .out11(out_5[11]),
    .out12(out_5[12]), .out13(out_5[13]), .out14(out_5[14]), .out15(out_5[15]), .sel(in_3), .en(in_1));
endmodule

module screen_ctrl (
  input  HSync,
  input  VSync,
  input  Red,
  input  Green,
  input  Blue,
  output [7:0] out_6,
  output [15:0] out_7
);

  wire and_1_out, and_2_out, comparator_1_lt, comparator_2_gt, comparator_3_gt, comparator_4_lt;
  wire [2:0] V_Counter_q_2, V_Counter_q_3;
  wire [3:0] V_Counter_q;
  wire [9:0] H_Counter_q;

  and and_1 (and_1_out, and_2_out, Red);
  Comparator #(.width(10), .mode("unsigned")) comparator_1 (
    .a(H_Counter_q), .b(10'h2f1), .lt(comparator_1_lt));  // open: gt, eq
  decoder decoder_1 (.in_1(and_1_out), .in_2(H_Counter_q[2:0]), .in_3(V_Counter_q), .out_4(out_6), .out_5(out_7));
  and and_2 (and_2_out, comparator_1_lt, comparator_2_gt, comparator_3_gt, comparator_4_lt);
  Comparator #(.width(10), .mode("unsigned")) comparator_2 (
    .a(H_Counter_q), .b(10'h70), .gt(comparator_2_gt));  // open: eq, lt
  Counter #(.width(10), .max('h207)) V_Counter (
    .count(1'b1), .Q({V_Counter_q_3, V_Counter_q_2, V_Counter_q}), .clk(VSync));  // open: load, D, carry, clr
  Comparator #(.width(10), .mode("unsigned")) comparator_3 (
    .a({V_Counter_q_3, V_Counter_q_2, V_Counter_q}), .b(10'h24), .gt(comparator_3_gt));  // open: eq, lt
  Counter #(.width(10), .max('h3a0)) H_Counter (
    .count(1'b1), .Q(H_Counter_q), .clk(HSync));  // open: load, D, carry, clr
  Comparator #(.width(10), .mode("unsigned")) comparator_4 (
    .a({V_Counter_q_3, V_Counter_q_2, V_Counter_q}), .b(10'h205), .lt(comparator_4_lt));  // open: gt, eq
endmodule
