// Logisim project ALL.circ as structural Verilog: 1 circuit, main circuit ALL
module ALL (
  input  IPae,
  input  IPae_2,
  output [3:0] out_3,
  output [15:0] DATAout,
  output [3:0] out_5,
  output CFout,
  output ZFout
);

  wire clock_1_out, decoder_1_out0, decoder_1_out1, decoder_1_out2, decoder_1_out3, decoder_1_out4,
       decoder_1_out5, decoder_1_out6, decoder_1_out7, decoder_1_out8, decoder_1_out9, decoder_1_out10,
       decoder_1_out11, decoder_1_out12, decoder_2_out0, decoder_2_out1, decoder_2_out2, decoder_2_out3,
       decoder_2_out4, decoder_2_out5, decoder_2_out6, decoder_2_out7, decoder_2_out8, decoder_2_out9,
       decoder_2_out10, decoder_2_out12, main_1_ivre, main_1_sele, main_1_zfe, main_1_zfe_2, main_2_carry,
       main_2_zf, not_1_out, not_2_out, or_1_out, or_2_out, or_3_out;
  wire [3:0] main_1_out_11;
  wire [8:0] main_1_romad;
  wire [15:0] controlled_buffer_1_out, controlled_buffer_13_out, IP_q, IV_q, main_1_ivout, main_2_z, MD_q,
       MP_q, R1_q, R2_q, R3_q, R4_q, rom_1_data, SP_q, Y_q, Z_q;
  wire [23:0] IR_q, ram_1_data;

  assign controlled_buffer_1_out = decoder_2_out10 ? IP_q : 16'bz;  // Controlled_Buffer controlled_buffer_1
  not not_1 (not_1_out, decoder_2_out10);
  assign controlled_buffer_1_out = not_1_out ? MP_q : 16'bz;  // Controlled_Buffer controlled_buffer_2
  Decoder #(.select(4), .disabled(0)) decoder_1 (
    .out0(decoder_1_out0), .out1(decoder_1_out1), .out2(decoder_1_out2), .out3(decoder_1_out3),
    .out4(decoder_1_out4), .out5(decoder_1_out5), .out6(decoder_1_out6), .out7(decoder_1_out7),
    .out8(decoder_1_out8), .out9(decoder_1_out9), .out10(decoder_1_out10), .out11(decoder_1_out11),
    .out12(decoder_1_out12), .sel(out_5), .en(main_1_sele));  // open: out13, out14, out15
  Clock clock_1 (.out(clock_1_out));
  not not_2 (not_2_out, decoder_1_out10);
  or or_1 (or_1_out, IPae_2, decoder_1_out6);
  RAM #(.addrWidth(16), .dataWidth(24), .bus("separate")) ram_1 (
    .addr(controlled_buffer_1_out), .din({{8{1'b0}}, DATAout}), .data(ram_1_data), .str(decoder_1_out10),
    .clk(clock_1_out), .ld(not_2_out));  // open: sel, clr
  or or_2 (or_2_out, IPae, decoder_1_out7);
  Register #(.width(24)) IR (.D(ram_1_data), .en(decoder_1_out11), .Q(IR_q), .clk(clock_1_out));  // open: clr
  assign DATAout = decoder_2_out9 ? MD_q : 16'bz;  // Controlled_Buffer controlled_buffer_3
  Register #(.width(16)) MD (.D(ram_1_data[15:0]), .en(decoder_1_out9), .Q(MD_q), .clk(clock_1_out));  // open: clr
  assign DATAout = decoder_2_out7 ? IP_q : 16'bz;  // Controlled_Buffer controlled_buffer_4
  Register #(.width(16)) IP (.D(DATAout), .en(or_2_out), .Q(IP_q), .clk(clock_1_out));  // open: clr
  assign DATAout = decoder_2_out6 ? MP_q : 16'bz;  // Controlled_Buffer controlled_buffer_5
  Register #(.width(16)) MP (.D(DATAout), .en(or_1_out), .Q(MP_q), .clk(clock_1_out));  // open: clr
  Register #(.width(16)) R1 (.D(DATAout), .en(decoder_1_out0), .Q(R1_q), .clk(clock_1_out));  // open: clr
  assign DATAout = decoder_2_out0 ? R1_q : 16'bz;  // Controlled_Buffer controlled_buffer_6
  Register #(.width(16)) R2 (.D(DATAout), .en(decoder_1_out1), .Q(R2_q), .clk(clock_1_out));  // open: clr
  assign DATAout = decoder_2_out1 ? R2_q : 16'bz;  // Controlled_Buffer controlled_buffer_7
  Register #(.width(16)) R3 (.D(DATAout), .en(decoder_1_out2), .Q(R3_q), .clk(clock_1_out));  // open: clr
  assign DATAout = decoder_2_out2 ? R3_q : 16'bz;  // Controlled_Buffer controlled_buffer_8
  Register #(.width(16)) R4 (.D(DATAout), .en(decoder_1_out3), .Q(R4_q), .clk(clock_1_out));  // open: clr
  assign DATAout = decoder_2_out3 ? R4_q : 16'bz;  // Controlled_Buffer controlled_buffer_9
  assign DATAout = decoder_2_out4 ? Y_q : 16'bz;  // Controlled_Buffer controlled_buffer_10
  Register #(.width(16)) Y (.D(DATAout), .en(decoder_1_out4), .Q(Y_q), .clk(clock_1_out));  // open: clr
  ROM #(.addrWidth(9), .dataWidth(16)) rom_1 (.addr(main_1_romad), .data(rom_1_data));  // open: sel
  CUsel_main main_1 (
    .ROMin(rom_1_data), .READse(out_3), .WRITEsel(out_5), .out_11(main_1_out_11), .ZFe(main_1_zfe),
    .ZFe_2(main_1_zfe_2), .CLK(clock_1_out), .SELe(main_1_sele), .ROMad(main_1_romad), .IRin(IR_q),
    .IVout(main_1_ivout), .IVre(main_1_ivre), .ZFin(ZFout), .CFin(CFout));  // open: SELe_2
  assign DATAout = decoder_2_out8 ? IV_q : 16'bz;  // Controlled_Buffer controlled_buffer_11
  Register #(.width(16)) SP (.D(DATAout), .en(decoder_1_out12), .Q(SP_q), .clk(clock_1_out));  // open: clr
  assign DATAout = decoder_2_out12 ? SP_q : 16'bz;  // Controlled_Buffer controlled_buffer_12
  Register #(.width(16)) IV (.D(main_1_ivout), .en(or_3_out), .Q(IV_q), .clk(clock_1_out));  // open: clr
  or or_3 (or_3_out, main_1_ivre, decoder_1_out8);
  assign controlled_buffer_13_out = decoder_1_out5 ? DATAout : 16'bz;  // Controlled_Buffer controlled_buffer_13
  Decoder #(.select(4), .disabled(0)) decoder_2 (
    .out0(decoder_2_out0), .out1(decoder_2_out1), .out2(decoder_2_out2), .out3(decoder_2_out3),
    .out4(decoder_2_out4), .out5(decoder_2_out5), .out6(decoder_2_out6), .out7(decoder_2_out7),
    .out8(decoder_2_out8), .out9(decoder_2_out9), .out10(decoder_2_out10), .out12(decoder_2_out12),
    .sel(out_3), .en(main_1_sele));  // open: out11, out13, out14, out15
  assign DATAout = decoder_2_out5 ? Z_q : 16'bz;  // Controlled_Buffer controlled_buffer_14
  ALU_main main_2 (
    .R(controlled_buffer_13_out), .Y(Y_q), .SEL(main_1_out_11), .Carry(main_2_carry), .Z(main_2_z),
    .ZF(main_2_zf));
  Register #(.width(16)) Z (.D(main_2_z), .en(decoder_1_out5), .Q(Z_q), .clk(clock_1_out));  // open: clr
  Register #(.width(1)) register_1 (.D(main_2_carry), .en(main_1_zfe), .Q(CFout), .clk(clock_1_out));  // open: clr
  Register #(.width(1)) register_2 (.D(main_2_zf), .en(main_1_zfe_2), .Q(ZFout), .clk(clock_1_out));  // open: clr

  // Notes on the sheet:
  //   contents of rom_1 (hex, n*v repeats v):
  //   8ab0 8ab0 9040 2050 b500 8752 8572 ffff 8*0 8ab0 8ab0 9040 2050 b500 8752 8572 ffff 8*0 8ab0 8ab0
  //   2050 b500 8752 8572 ffff 9*0 8ab0 8ab0 2050 b500 8752 8572 ffff 9*0 8ab0 8ab0 9040 2050 b500 8752
  //   8572 ffff 8*0 8ab0 8ab0 9040 2050 b500 8752 8572 ffff 8*0 8ab0 8ab0 9040 2050 b500 8752 8572 ffff
  //   8*0 8ab0 8ab0 9040 2050 b500 8752 8572 ffff 8*0 8ab0 8ab0 9040 2050 b500 8752 8572 ffff 8*0 8ab0
  //   8ab0 9040 2050 b500 8752 8572 ffff 8*0 8ab0 8ab0 9040 2050 b500 8752 8572 ffff 8*0 8ab0 8ab0 9040
  //   2050 b500 8752 8572 ffff 8*0 8ab0 8ab0 9040 2050 b500 8752 8572 ffff 8*0 8ab0 8ab0 9040 2050 b500
  //   8752 8572 ffff 8*0 8ab0 8ab0 9040 2050 b500 8752 8572 ffff 8*0 8ab0 8ab0 9040 2050 b500 8752 8572
  //   ffff 8*0 8ab0 8ab0 c000 8752 8572 ffff 10*0 8ab0 8ab0 a040 c000 d400 8752 8572 ffff 8*0 8ab0 8ab0
  //   9040 8750 8572 ffff 10*0 8ab0 8ab0 9040 a051 8752 8572 ffff 9*0 8ab0 8ab0 9060 8f90 b900 8752 8572
  //   ffff 8*0 8ab0 8ab0 9060 a0a0 8752 8572 ffff 9*0 8ab0 8ab0 9060 a051 a0a0 b900 8752 8572 ffff 7*0
  //   8ab0 8ab0 9040 8750 8572 ffff 10*0 8ab0 8ab0 9040 8750 8572 ffff 10*0 8ab0 8ab0 9040 8750 8572 ffff
  //   10*0 8ab0 8ab0 253 8520 9040 8750 8572 ffff 8*0 8ab0 8ab0 8c60 a0a0 8c53 85c0 8752 8572 ffff 7*0
  //   8ab0 8ab0 8c52 85c0 8c60 8f90 b900 8752 8572 ffff 6*0 8ab0 8ab0 8c60 87a0 9070 8c53 85c0 ffff 8*0
  //   8ab0 8ab0 8c52 85c0 8c60 8f90 8970 8752 8572 ffff
endmodule
