// Logisim project ALU-Outer.circ as structural Verilog: 2 circuits, main circuit main
module main (
  input  FlagEnable,
  input  [3:0] SEL,
  input  ALUEnable,
  input  [15:0] R,
  input  [15:0] Y,
  input  CLK,
  output CarryFlag,
  output ZeroFlag,
  output [15:0] Z
);

  wire alu_1_carry, alu_1_carryenable, alu_1_zf, and_1_out, and_2_out;
  wire [15:0] alu_1_z;

  ALU alu_1 (.R(R), .Y(Y), .SEL(SEL), .Carry(alu_1_carry), .CarryEnable(alu_1_carryenable), .Z(alu_1_z), .ZF(alu_1_zf));
  Register #(.width(16)) u_Z (.D(alu_1_z), .en(ALUEnable), .Q(Z), .clk(CLK));  // open: clr
  and and_1 (and_1_out, FlagEnable, ALUEnable, alu_1_carryenable);
  and and_2 (and_2_out, FlagEnable, ALUEnable);
  Register #(.width(1)) u_CarryFlag (.D(alu_1_carry), .en(and_1_out), .Q(CarryFlag), .clk(CLK));  // open: clr
  Register #(.width(1)) u_ZeroFlag (.D(alu_1_zf), .en(and_2_out), .Q(ZeroFlag), .clk(CLK));  // open: clr
endmodule

module ALU (
  input  [15:0] R,
  input  [15:0] Y,
  input  [3:0] SEL,
  output Carry,
  output CarryEnable,
  output [15:0] Z,
  output ZF
);

  wire adder_1_cout, adder_2_cout, subtractor_1_bout, subtractor_2_bout;
  wire [15:0] adder_1_out, adder_2_out, and_1_out, divider_1_out, divider_1_rem, multiplier_1_out,
       negator_1_out, not_1_out, or_1_out, shifter_1_out, shifter_2_out, shifter_3_out, shifter_4_out,
       subtractor_1_out, subtractor_2_out, xor_1_out;

  Adder #(.width(16)) adder_1 (.a(R), .b(Y), .out(adder_1_out), .cout(adder_1_cout));  // open: cin
  Subtractor #(.width(16)) subtractor_1 (.a(R), .b(Y), .out(subtractor_1_out), .bout(subtractor_1_bout));  // open: bin
  Adder #(.width(16)) adder_2 (.a(R), .b(16'h1), .out(adder_2_out), .cout(adder_2_cout));  // open: cin
  Subtractor #(.width(16)) subtractor_2 (
    .a(R), .b(16'h1), .out(subtractor_2_out), .bout(subtractor_2_bout));  // open: bin
  assign and_1_out = R & Y;  // AND_Gate and_1, 16 bits wide
  assign or_1_out = R | Y;  // OR_Gate or_1, 16 bits wide
  assign xor_1_out = R ^ Y;  // XOR_Gate xor_1, 16 bits wide
  assign not_1_out = ~R;  // NOT_Gate not_1, 16 bits wide
  Shifter #(.width(16)) shifter_1 (.in(R), .\dist (Y[3:0]), .out(shifter_1_out));
  Shifter #(.width(16), .shift("lr")) shifter_2 (.in(R), .\dist (Y[3:0]), .out(shifter_2_out));
  Shifter #(.width(16), .shift("rl")) shifter_3 (.in(R), .\dist (Y[3:0]), .out(shifter_3_out));
  Shifter #(.width(16), .shift("rr")) shifter_4 (.in(R), .\dist (Y[3:0]), .out(shifter_4_out));
  Negator #(.width(16)) negator_1 (.in(R), .out(negator_1_out));
  Multiplier #(.width(16)) multiplier_1 (.a(R), .b(Y), .out(multiplier_1_out));  // open: cin, cout
  Divider #(.width(16)) divider_1 (.a(R), .b(Y), .out(divider_1_out), .rem(divider_1_rem));  // open: upper
  Multiplexer #(.select(2), .disabled(0)) multiplexer_1 (
    .in0(adder_1_cout), .in1(subtractor_1_bout), .in2(adder_2_cout), .in3(subtractor_2_bout), .out(Carry),
    .sel(SEL[1:0]), .en(CarryEnable));
  nor nor_1 (CarryEnable, SEL[3], SEL[2]);
  Multiplexer #(.select(4), .width(16), .enable("false")) multiplexer_2 (
    .in0(adder_1_out), .in1(subtractor_1_out), .in2(adder_2_out), .in3(subtractor_2_out), .in4(and_1_out),
    .in5(or_1_out), .in6(xor_1_out), .in7(not_1_out), .in8(shifter_1_out), .in9(shifter_2_out),
    .in10(shifter_3_out), .in11(shifter_4_out), .in12(negator_1_out), .in13(multiplier_1_out),
    .in14(divider_1_out), .in15(divider_1_rem), .out(Z), .sel(SEL));
  nor nor_2 (ZF, Z[0], Z[1], Z[2], Z[3], Z[4], Z[5], Z[6], Z[7], Z[8], Z[9], Z[10], Z[11], Z[12], Z[13], Z[14], Z[15]);
endmodule
