// Logisim project BUSnew.circ as structural Verilog: 1 circuit, main circuit main
module main (
  input  SELe,
  input  CFe,
  input  ZFe,
  input  [3:0] WRITEsel,
  input  [3:0] ALUsel,
  input  [3:0] READsel,
  input  CLK,
  input  IPae,
  input  IPae_2,
  input  [15:0] IVin,
  input  IVrin,
  output [23:0] IRout,
  output [15:0] DATAout,
  output CFout,
  output ZFout
);

  wire decoder_1_out0, decoder_1_out1, decoder_1_out2, decoder_1_out3, decoder_1_out4, decoder_1_out5,
       decoder_1_out6, decoder_1_out7, decoder_1_out8, decoder_1_out9, decoder_1_out10, decoder_1_out11,
       decoder_1_out12, decoder_2_out0, decoder_2_out1, decoder_2_out2, decoder_2_out3, decoder_2_out4,
       decoder_2_out5, decoder_2_out6, decoder_2_out7, decoder_2_out8, decoder_2_out9, decoder_2_out10,
       decoder_2_out12, main_1_carry, main_1_zf, not_1_out, not_2_out, or_1_out, or_2_out, or_3_out;
  wire [15:0] controlled_buffer_1_out, controlled_buffer_13_out, IP_q, IV_q, main_1_z, MD_q, MP_q, R1_q,
       R2_q, R3_q, R4_q, SP_q, Y_q, Z_q;
  wire [23:0] ram_1_data;

  assign controlled_buffer_1_out = decoder_2_out10 ? IP_q : 16'bz;  // Controlled_Buffer controlled_buffer_1
  not not_1 (not_1_out, decoder_2_out10);
  assign controlled_buffer_1_out = not_1_out ? MP_q : 16'bz;  // Controlled_Buffer controlled_buffer_2
  Decoder #(.select(4), .disabled(0)) decoder_1 (
    .out0(decoder_1_out0), .out1(decoder_1_out1), .out2(decoder_1_out2), .out3(decoder_1_out3),
    .out4(decoder_1_out4), .out5(decoder_1_out5), .out6(decoder_1_out6), .out7(decoder_1_out7),
    .out8(decoder_1_out8), .out9(decoder_1_out9), .out10(decoder_1_out10), .out11(decoder_1_out11),
    .out12(decoder_1_out12), .sel(WRITEsel), .en(SELe));  // open: out13, out14, out15
  not not_2 (not_2_out, decoder_1_out10);
  RAM #(.addrWidth(16), .dataWidth(24), .bus("separate")) ram_1 (
    .addr(controlled_buffer_1_out), .din({{8{1'b0}}, DATAout}), .data(ram_1_data), .str(decoder_1_out10),
    .clk(CLK), .ld(not_2_out));  // open: sel, clr
  or or_1 (or_1_out, IPae, decoder_1_out7);
  or or_2 (or_2_out, IPae_2, decoder_1_out6);
  Register #(.width(24)) IR (.D(ram_1_data), .en(decoder_1_out11), .Q(IRout), .clk(CLK));  // open: clr
  Register #(.width(16)) MD (.D(ram_1_data[15:0]), .en(decoder_1_out9), .Q(MD_q), .clk(CLK));  // open: clr
  Register #(.width(16)) IP (.D(DATAout), .en(or_1_out), .Q(IP_q), .clk(CLK));  // open: clr
  Register #(.width(16)) MP (.D(DATAout), .en(or_2_out), .Q(MP_q), .clk(CLK));  // open: clr
  Register #(.width(16)) R1 (.D(DATAout), .en(decoder_1_out0), .Q(R1_q), .clk(CLK));  // open: clr
  Register #(.width(16)) R2 (.D(DATAout), .en(decoder_1_out1), .Q(R2_q), .clk(CLK));  // open: clr
  Register #(.width(16)) R3 (.D(DATAout), .en(decoder_1_out2), .Q(R3_q), .clk(CLK));  // open: clr
  Register #(.width(16)) R4 (.D(DATAout), .en(decoder_1_out3), .Q(R4_q), .clk(CLK));  // open: clr
  Register #(.width(16)) Y (.D(DATAout), .en(decoder_1_out4), .Q(Y_q), .clk(CLK));  // open: clr
  assign DATAout = decoder_2_out9 ? MD_q : 16'bz;  // Controlled_Buffer controlled_buffer_3
  assign DATAout = decoder_2_out7 ? IP_q : 16'bz;  // Controlled_Buffer controlled_buffer_4
  assign DATAout = decoder_2_out6 ? MP_q : 16'bz;  // Controlled_Buffer controlled_buffer_5
  assign DATAout = decoder_2_out8 ? IV_q : 16'bz;  // Controlled_Buffer controlled_buffer_6
  assign DATAout = decoder_2_out0 ? R1_q : 16'bz;  // Controlled_Buffer controlled_buffer_7
  Register #(.width(16)) SP (.D(DATAout), .en(decoder_1_out12), .Q(SP_q), .clk(CLK));  // open: clr
  assign DATAout = decoder_2_out1 ? R2_q : 16'bz;  // Controlled_Buffer controlled_buffer_8
  assign DATAout = decoder_2_out12 ? SP_q : 16'bz;  // Controlled_Buffer controlled_buffer_9
  assign DATAout = decoder_2_out2 ? R3_q : 16'bz;  // Controlled_Buffer controlled_buffer_10
  assign DATAout = decoder_2_out3 ? R4_q : 16'bz;  // Controlled_Buffer controlled_buffer_11
  assign DATAout = decoder_2_out4 ? Y_q : 16'bz;  // Controlled_Buffer controlled_buffer_12
  or or_3 (or_3_out, IVrin, decoder_1_out8);
  assign controlled_buffer_13_out = decoder_1_out5 ? DATAout : 16'bz;  // Controlled_Buffer controlled_buffer_13
  Decoder #(.select(4), .disabled(0)) decoder_2 (
    .out0(decoder_2_out0), .out1(decoder_2_out1), .out2(decoder_2_out2), .out3(decoder_2_out3),
    .out4(decoder_2_out4), .out5(decoder_2_out5), .out6(decoder_2_out6), .out7(decoder_2_out7),
    .out8(decoder_2_out8), .out9(decoder_2_out9), .out10(decoder_2_out10), .out12(decoder_2_out12),
    .sel(ALUsel), .en(SELe));  // open: out11, out13, out14, out15
  Register #(.width(16)) IV (.D(IVin), .en(or_3_out), .Q(IV_q), .clk(CLK));  // open: clr
  assign DATAout = decoder_2_out5 ? Z_q : 16'bz;  // Controlled_Buffer controlled_buffer_14
  ALU_main main_1 (
    .R(controlled_buffer_13_out), .Y(Y_q), .SEL(READsel), .Carry(main_1_carry), .Z(main_1_z), .ZF(main_1_zf));
  Register #(.width(16)) Z (.D(main_1_z), .en(decoder_1_out5), .Q(Z_q), .clk(CLK));  // open: clr
  Register #(.width(1)) register_1 (.D(main_1_carry), .en(CFe), .Q(CFout), .clk(CLK));  // open: clr
  Register #(.width(1)) register_2 (.D(main_1_zf), .en(ZFe), .Q(ZFout), .clk(CLK));  // open: clr
endmodule
