// Logisim project Bus16.circ as structural Verilog: 1 circuit, main circuit main
module main (
  input  OUTe,
  input  IPae,
  input  [3:0] OUTsel,
  input  IPae_2,
  input  [15:0] IRin,
  input  IRae,
  input  INe,
  input  [3:0] INsel,
  input  CFe,
  input  ZFe,
  input  [3:0] ALUsel,
  input  CLK,
  output [15:0] IPout,
  output [15:0] MPout,
  output [15:0] DATAout,
  output CFout,
  output ZFout
);

  wire decoder_1_out0, decoder_1_out1, decoder_1_out2, decoder_1_out3, decoder_1_out4, decoder_1_out5,
       decoder_1_out6, decoder_1_out7, decoder_1_out8, decoder_2_out0, decoder_2_out1, decoder_2_out2,
       decoder_2_out3, decoder_2_out4, decoder_2_out5, decoder_2_out6, decoder_2_out7, decoder_2_out8,
       main_1_carry, main_1_zf, or_1_out, or_2_out, or_3_out;
  wire [15:0] controlled_buffer_9_out, IR_q, main_1_z, R1_q, R2_q, R3_q, R4_q, Y_q, Z_q;

  Decoder #(.select(4)) decoder_1 (
    .out0(decoder_1_out0), .out1(decoder_1_out1), .out2(decoder_1_out2), .out3(decoder_1_out3),
    .out4(decoder_1_out4), .out5(decoder_1_out5), .out6(decoder_1_out6), .out7(decoder_1_out7),
    .out8(decoder_1_out8), .sel(INsel), .en(INe));  // open: out9, out10, out11, out12, out13, out14, out15
  or or_1 (or_1_out, IPae, decoder_1_out7);
  or or_2 (or_2_out, IPae_2, decoder_1_out6);
  Register #(.width(16)) IP (.D(DATAout), .en(or_1_out), .Q(IPout), .clk(CLK));  // open: clr
  Register #(.width(16)) MP (.D(DATAout), .en(or_2_out), .Q(MPout), .clk(CLK));  // open: clr
  Register #(.width(16)) R1 (.D(DATAout), .en(decoder_1_out0), .Q(R1_q), .clk(CLK));  // open: clr
  Register #(.width(16)) R2 (.D(DATAout), .en(decoder_1_out1), .Q(R2_q), .clk(CLK));  // open: clr
  Register #(.width(16)) R3 (.D(DATAout), .en(decoder_1_out2), .Q(R3_q), .clk(CLK));  // open: clr
  Register #(.width(16)) R4 (.D(DATAout), .en(decoder_1_out3), .Q(R4_q), .clk(CLK));  // open: clr
  Register #(.width(16)) Y (.D(DATAout), .en(decoder_1_out4), .Q(Y_q), .clk(CLK));  // open: clr
  assign DATAout = decoder_2_out7 ? IPout : 16'bz;  // Controlled_Buffer controlled_buffer_1
  assign DATAout = decoder_2_out6 ? MPout : 16'bz;  // Controlled_Buffer controlled_buffer_2
  assign DATAout = decoder_2_out8 ? IR_q : 16'bz;  // Controlled_Buffer controlled_buffer_3
  assign DATAout = decoder_2_out0 ? R1_q : 16'bz;  // Controlled_Buffer controlled_buffer_4
  assign DATAout = decoder_2_out1 ? R2_q : 16'bz;  // Controlled_Buffer controlled_buffer_5
  assign DATAout = decoder_2_out2 ? R3_q : 16'bz;  // Controlled_Buffer controlled_buffer_6
  assign DATAout = decoder_2_out3 ? R4_q : 16'bz;  // Controlled_Buffer controlled_buffer_7
  assign DATAout = decoder_2_out4 ? Y_q : 16'bz;  // Controlled_Buffer controlled_buffer_8
  or or_3 (or_3_out, IRae, decoder_1_out8);
  assign controlled_buffer_9_out = decoder_1_out5 ? DATAout : 16'bz;  // Controlled_Buffer controlled_buffer_9
  Register #(.width(16)) IR (.D(IRin), .en(or_3_out), .Q(IR_q), .clk(CLK));  // open: clr
  assign DATAout = decoder_2_out5 ? Z_q : 16'bz;  // Controlled_Buffer controlled_buffer_10
  ALU_main main_1 (
    .R(controlled_buffer_9_out), .Y(Y_q), .SEL(ALUsel), .Carry(main_1_carry), .Z(main_1_z), .ZF(main_1_zf));
  Decoder #(.select(4)) decoder_2 (
    .out0(decoder_2_out0), .out1(decoder_2_out1), .out2(decoder_2_out2), .out3(decoder_2_out3),
    .out4(decoder_2_out4), .out5(decoder_2_out5), .out6(decoder_2_out6), .out7(decoder_2_out7),
    .out8(decoder_2_out8), .sel(OUTsel), .en(OUTe));  // open: out9, out10, out11, out12, out13, out14, out15
  Register #(.width(16)) Z (.D(main_1_z), .en(decoder_1_out5), .Q(Z_q), .clk(CLK));  // open: clr
  Register #(.width(1)) register_1 (.D(main_1_carry), .en(CFe), .Q(CFout), .clk(CLK));  // open: clr
  Register #(.width(1)) register_2 (.D(main_1_zf), .en(ZFe), .Q(ZFout), .clk(CLK));  // open: clr
endmodule
