// Logisim project BusModule.circ as structural Verilog: 1 circuit, main circuit main
module main (
  input  [3:0] ReadSel,
  input  OUTe,
  input  [15:0] IV_In,
  input  [3:0] WriteSel,
  input  INe,
  input  [15:0] MDin,
  input  [15:0] Z_In,
  input  [15:0] DATAin,
  input  CLK,
  output InsChange,
  output [15:0] IPout,
  output [15:0] MPout,
  output [15:0] MDout,
  output MemWrite,
  output MemRead,
  output Z_Enable,
  output [15:0] R_Out,
  output [15:0] Y_out,
  output DataOutEnable,
  output [15:0] DATAout
);

  wire decoder_1_out0, decoder_1_out1, decoder_1_out2, decoder_1_out3, decoder_1_out4, decoder_1_out6,
       decoder_1_out12, decoder_2_out0, decoder_2_out1, decoder_2_out2, decoder_2_out3, decoder_2_out4,
       decoder_2_out5, decoder_2_out6, decoder_2_out7, decoder_2_out8, decoder_2_out10, decoder_2_out12;
  wire [15:0] R1_q, R2_q, R3_q, R4_q, SP_q;

  Decoder #(.select(4), .disabled(0)) decoder_1 (
    .out0(decoder_1_out0), .out1(decoder_1_out1), .out2(decoder_1_out2), .out3(decoder_1_out3),
    .out4(decoder_1_out4), .out5(Z_Enable), .out6(decoder_1_out6), .out7(InsChange), .out9(MemWrite),
    .out10(DataOutEnable), .out12(decoder_1_out12), .sel(WriteSel), .en(INe));  // open: out8, out11, out13, out14, out15
  assign DATAout = decoder_2_out10 ? DATAin : 16'bz;  // Controlled_Buffer controlled_buffer_1
  Register #(.width(16)) R1 (.D(DATAout), .en(decoder_1_out0), .Q(R1_q), .clk(CLK));  // open: clr
  Register #(.width(16)) R2 (.D(DATAout), .en(decoder_1_out1), .Q(R2_q), .clk(CLK));  // open: clr
  Register #(.width(16)) R3 (.D(DATAout), .en(decoder_1_out2), .Q(R3_q), .clk(CLK));  // open: clr
  Register #(.width(16)) R4 (.D(DATAout), .en(decoder_1_out3), .Q(R4_q), .clk(CLK));  // open: clr
  Register #(.width(16)) Y (.D(DATAout), .en(decoder_1_out4), .Q(Y_out), .clk(CLK));  // open: clr
  assign DATAout = decoder_2_out8 ? IV_In : 16'bz;  // Controlled_Buffer controlled_buffer_2
  assign DATAout = decoder_2_out0 ? R1_q : 16'bz;  // Controlled_Buffer controlled_buffer_3
  assign DATAout = decoder_2_out1 ? R2_q : 16'bz;  // Controlled_Buffer controlled_buffer_4
  assign DATAout = decoder_2_out2 ? R3_q : 16'bz;  // Controlled_Buffer controlled_buffer_5
  assign DATAout = decoder_2_out3 ? R4_q : 16'bz;  // Controlled_Buffer controlled_buffer_6
  assign DATAout = decoder_2_out4 ? Y_out : 16'bz;  // Controlled_Buffer controlled_buffer_7
  assign DATAout = decoder_2_out5 ? Z_In : 16'bz;  // Controlled_Buffer controlled_buffer_8
  Register #(.width(16)) IP (.D(DATAout), .en(InsChange), .Q(IPout), .clk(CLK));  // open: clr
  Register #(.width(16)) MP (.D(DATAout), .en(decoder_1_out6), .Q(MPout), .clk(CLK));  // open: clr
  assign DATAout = MemRead ? MDin : 16'bz;  // Controlled_Buffer controlled_buffer_9
  Register #(.width(16)) SP (.D(DATAout), .en(decoder_1_out12), .Q(SP_q), .clk(CLK));  // open: clr
  assign DATAout = decoder_2_out7 ? IPout : 16'bz;  // Controlled_Buffer controlled_buffer_10
  assign DATAout = decoder_2_out6 ? MPout : 16'bz;  // Controlled_Buffer controlled_buffer_11
  assign DATAout = decoder_2_out12 ? SP_q : 16'bz;  // Controlled_Buffer controlled_buffer_12
  Decoder #(.select(4), .disabled(0)) decoder_2 (
    .out0(decoder_2_out0), .out1(decoder_2_out1), .out2(decoder_2_out2), .out3(decoder_2_out3),
    .out4(decoder_2_out4), .out5(decoder_2_out5), .out6(decoder_2_out6), .out7(decoder_2_out7),
    .out8(decoder_2_out8), .out9(MemRead), .out10(decoder_2_out10), .out12(decoder_2_out12), .sel(ReadSel),
    .en(OUTe));  // open: out11, out13, out14, out15

  assign MDout = DATAout;
  assign R_Out = DATAout;
endmodule
