// Logisim project CUModule.circ as structural Verilog: 1 circuit, main circuit main
module main (
  input  [15:0] IRomIn,
  input  [15:0] IRomAddressIn,
  output [15:0] IVout,
  output [15:0] IRomAddress
);

  Register #(.width(16)) IRegister (.D(IRomIn));  // open: en, Q, clk, clr

  assign IRomAddress = IRomAddressIn;
  assign IVout = IRomIn;
endmodule
