// Logisim project CUsel.circ as structural Verilog: 2 circuits, main circuit main
module main (
  input  [23:0] IRin,
  input  ZFin,
  input  [15:0] ROMin,
  input  CFin,
  input  CLK,
  output [15:0] IVout,
  output IVre,
  output [8:0] ROMad,
  output SELe,
  output ZFe,
  output [3:0] out_11,
  output ZFe_2,
  output [3:0] READse,
  output [3:0] WRITEsel,
  output SELe_2
);

  wire and_1_out, and_2_out, and_3_out, comparator_1_eq, iffsel_1_out_4, nor_1_out, not_3_out;
  wire [3:0] multiplexer_2_out, multiplexer_4_out;
  wire [15:0] MI_q;

  not not_1 (SELe, 1'b0);
  Counter #(.width(4), .max('hf)) counter_1 (
    .load(and_1_out), .D(4'b0000), .count(SELe), .Q(ROMad[3:0]), .clk(CLK), .clr(and_1_out));  // open: carry
  and and_1 (and_1_out, MI_q[15], MI_q[14], MI_q[13], MI_q[12]);
  Register #(.width(16)) MI (.D(ROMin), .en(SELe), .Q(MI_q), .clk(CLK));  // open: clr
  Multiplexer #(.select(3), .width(4), .enable("false")) multiplexer_1 (
    .in0(MI_q[11:8]), .in1(multiplexer_4_out), .in2(multiplexer_2_out), .in3(MI_q[11:8]),
    .in4(multiplexer_4_out), .in5(MI_q[11:8]), .in6(multiplexer_2_out), .in7(MI_q[11:8]), .out(READse),
    .sel(MI_q[14:12]));
  Multiplexer #(.width(4), .enable("false")) multiplexer_2 (
    .in0({2'b00, IRin[18:17]}), .in1(4'b1000), .out(multiplexer_2_out), .sel(iffsel_1_out_4));
  Multiplexer #(.select(3), .width(4), .enable("false")) multiplexer_3 (
    .in0(MI_q[7:4]), .in1(MI_q[7:4]), .in2(MI_q[7:4]), .in3(multiplexer_2_out), .in4(multiplexer_2_out),
    .in5(multiplexer_4_out), .in6(multiplexer_4_out), .in7(MI_q[7:4]), .out(WRITEsel), .sel(MI_q[14:12]));
  Multiplexer #(.width(4), .enable("false")) multiplexer_4 (
    .in0({2'b00, IRin[15:14]}), .in1(4'b1000), .out(multiplexer_4_out), .sel(IRin[16]));
  Multiplexer #(.width(4), .enable("false")) multiplexer_5 (
    .in0(IRin[22:19]), .in1(MI_q[3:0]), .out(out_11), .sel(MI_q[15]));
  Comparator #(.width(4)) comparator_1 (.a(WRITEsel), .b(READse), .eq(comparator_1_eq));  // open: gt, lt
  Multiplexer #(.width(16), .enable("false")) multiplexer_6 (
    .in0(IRin[15:0]), .in1(16'h1), .out(IVout), .sel(iffsel_1_out_4));
  not not_2 (SELe_2, comparator_1_eq);
  and and_2 (and_2_out, IRin[23], ~IRin[22], ~IRin[21], IRin[20], IRin[19], ~MI_q[3], ~MI_q[2], ~MI_q[1], MI_q[0]);  // AND_Gate
  nor nor_1 (nor_1_out, out_11[2], out_11[3], MI_q[15]);
  not not_3 (not_3_out, MI_q[15]);
  IFFsel iffsel_1 (.in_1(IRin[23:19]), .out_4(iffsel_1_out_4), .ZFin(ZFin), .CFin(CFin));
  and and_3 (and_3_out, IRin[23], IRin[22], ~IRin[21], IRin[20], ~IRin[19], ~MI_q[3], ~MI_q[2], MI_q[1], MI_q[0]);  // AND_Gate
  or or_1 (ZFe, and_2_out, nor_1_out);
  or or_2 (ZFe_2, and_2_out, and_3_out, not_3_out);

  assign IVre = IRin[16];
  assign ROMad[8:4] = IRin[23:19];
endmodule

module IFFsel (
  input  [4:0] in_1,
  input  ZFin,
  input  CFin,
  output out_4
);

  wire and_1_out, and_2_out, and_3_out, and_4_out;

  and and_1 (and_1_out, in_1[4], ~in_1[3], in_1[2], in_1[1], in_1[0], ~ZFin);  // AND_Gate
  and and_2 (and_2_out, in_1[4], in_1[3], ~in_1[2], ~in_1[1], ~in_1[0], CFin);  // AND_Gate
  or or_1 (out_4, and_1_out, and_2_out, and_3_out, and_4_out);
  and and_3 (and_3_out, in_1[4], in_1[3], ~in_1[2], ~in_1[1], in_1[0], ~CFin);  // AND_Gate
  and and_4 (and_4_out, in_1[4], in_1[3], ~in_1[2], in_1[1], ~in_1[0], ~ZFin);  // AND_Gate
endmodule
