// Logisim project ASyncRamSubInt.circ as structural Verilog: 4 circuits, main circuit main
module main (
  input  [19:0] Address,
  input  [1:0] WSSel,
  input  WE,
  input  CE,
  input  ErrorIn,
  input  [7:0] B3Din,
  input  [7:0] B2Din,
  input  [7:0] B1Din,
  input  [7:0] B0Din,
  output ErrorOut,
  output [7:0] B3Dout,
  output [7:0] B2Dout,
  output [7:0] B1Dout,
  output [7:0] B0Dout,
  output B3F,
  output B2F,
  output B1F,
  output B0F
);

  wire nand_1_out, not_1_out, or_1_out, ramadressctrl_1_b0, ramadressctrl_1_b1, ramadressctrl_1_b2,
       ramadressctrl_1_b3, ramadressctrl_1_ordersel0, ramadressctrl_1_ordersel1;
  wire [15:0] Lower_Word_dout, shiftctrl_1_lwdin, shiftctrl_1_uwdin, Upper_Word_dout;
  wire [17:0] ofctrl_1_adressout;

  OFCtrl ofctrl_1 (.AdressIn(Address[19:2]), .ERR(ErrorIn), .AdressOut(ofctrl_1_adressout));
  UnitSRAM_simulator_main Upper_Word (
    .CE(nand_1_out), .UB(ramadressctrl_1_b3), .LB(ramadressctrl_1_b2), .WE(WE), .OE(not_1_out),
    .Address(ofctrl_1_adressout), .Dout(Upper_Word_dout), .Din(shiftctrl_1_uwdin));
  not not_1 (not_1_out, WE);
  RamAdressCtrl ramadressctrl_1 (
    .WSS1(WSSel[1]), .WSS0(WSSel[0]), .ADRS1(Address[1]), .ADRS0(Address[0]), .ERRin(ErrorIn),
    .B0(ramadressctrl_1_b0), .B1(ramadressctrl_1_b1), .B2(ramadressctrl_1_b2), .B3(ramadressctrl_1_b3),
    .ERR(ErrorOut), .OrderSel0(ramadressctrl_1_ordersel0), .OrderSel1(ramadressctrl_1_ordersel1));
  UnitSRAM_simulator_main Lower_Word (
    .CE(nand_1_out), .UB(ramadressctrl_1_b1), .LB(ramadressctrl_1_b0), .WE(WE), .OE(not_1_out),
    .Address(ofctrl_1_adressout), .Dout(Lower_Word_dout), .Din(shiftctrl_1_lwdin));
  ShiftCtrl shiftctrl_1 (
    .UWDin(shiftctrl_1_uwdin), .UWDout(Upper_Word_dout), .LWDin(shiftctrl_1_lwdin), .LWDout(Lower_Word_dout),
    .OrderSel1(ramadressctrl_1_ordersel1), .OrderSel0(ramadressctrl_1_ordersel0), .B3(ramadressctrl_1_b3),
    .B2(ramadressctrl_1_b2), .B1(ramadressctrl_1_b1), .B0(ramadressctrl_1_b0), .B3Dout(B3Dout),
    .B2Dout(B2Dout), .B1Dout(B1Dout), .B0Dout(B0Dout), .B3Din(B3Din), .B2Din(B2Din), .B1Din(B1Din),
    .B0Din(B0Din), .B3F(B3F), .B2F(B2F), .B1F(B1F), .B0F(B0F));
  or or_1 (or_1_out, WSSel[0], WSSel[1]);
  nand nand_1 (nand_1_out, or_1_out, CE);
endmodule

module RamAdressCtrl (
  input  WSS1,
  input  WSS0,
  input  ADRS1,
  input  ADRS0,
  input  ERRin,
  output B0,
  output B1,
  output B2,
  output B3,
  output ERR,
  output OrderSel0,
  output OrderSel1
);

  wire and_1_out, and_2_out, and_3_out, and_4_out, and_5_out, and_6_out, and_7_out, and_8_out, and_9_out,
       and_10_out, and_11_out, and_12_out, and_13_out, and_14_out, and_15_out, and_16_out, and_17_out,
       and_18_out, and_19_out, and_20_out, and_21_out, and_22_out, and_23_out, and_24_out, and_25_out,
       and_26_out, and_27_out, and_28_out, and_29_out, and_30_out, and_31_out, not_1_out, not_2_out,
       not_3_out, not_4_out, not_5_out, not_6_out, not_7_out, not_8_out, not_9_out, not_10_out, not_11_out,
       not_12_out, not_13_out, not_14_out, not_15_out, not_16_out, not_17_out, not_18_out, not_19_out,
       not_20_out, not_21_out, not_22_out, not_23_out, not_24_out, not_25_out, not_26_out, not_27_out,
       not_28_out, not_29_out, not_30_out, not_31_out, not_32_out, not_33_out, not_34_out, not_35_out,
       not_36_out, not_37_out, not_38_out, not_39_out, not_40_out, not_41_out, not_42_out, not_43_out,
       not_44_out;

  not not_1 (not_1_out, ADRS1);
  not not_2 (not_2_out, ADRS0);
  not not_3 (not_3_out, WSS0);
  not not_4 (not_4_out, WSS0);
  not not_5 (not_5_out, ADRS1);
  not not_6 (not_6_out, WSS1);
  not not_7 (not_7_out, ADRS1);
  not not_8 (not_8_out, ADRS1);
  not not_9 (not_9_out, ERRin);
  not not_10 (not_10_out, ADRS1);
  not not_11 (not_11_out, ADRS0);
  not not_12 (not_12_out, WSS0);
  not not_13 (not_13_out, ADRS1);
  not not_14 (not_14_out, WSS1);
  not not_15 (not_15_out, ADRS0);
  not not_16 (not_16_out, WSS0);
  not not_17 (not_17_out, ADRS0);
  not not_18 (not_18_out, ADRS0);
  not not_19 (not_19_out, ERRin);
  not not_20 (not_20_out, ADRS1);
  not not_21 (not_21_out, ERRin);
  not not_22 (not_22_out, ADRS1);
  not not_23 (not_23_out, ADRS0);
  not not_24 (not_24_out, WSS0);
  not not_25 (not_25_out, ADRS0);
  not not_26 (not_26_out, WSS0);
  not not_27 (not_27_out, ERRin);
  not not_28 (not_28_out, WSS1);
  not not_29 (not_29_out, ADRS1);
  not not_30 (not_30_out, ADRS0);
  not not_31 (not_31_out, ERRin);
  not not_32 (not_32_out, WSS0);
  not not_33 (not_33_out, ERRin);
  not not_34 (not_34_out, ERRin);
  not not_35 (not_35_out, ERRin);
  not not_36 (not_36_out, ADRS1);
  not not_37 (not_37_out, WSS1);
  not not_38 (not_38_out, WSS0);
  not not_39 (not_39_out, ADRS0);
  not not_40 (not_40_out, WSS1);
  not not_41 (not_41_out, WSS0);
  not not_42 (not_42_out, ADRS1);
  not not_43 (not_43_out, ADRS0);
  not not_44 (not_44_out, ADRS0);
  and and_1 (and_1_out, not_1_out, not_2_out);
  and and_2 (and_2_out, not_3_out, ADRS1, ADRS0, ERRin);
  and and_3 (and_3_out, WSS1, WSS0, ERRin);
  and and_4 (and_4_out, not_4_out, not_5_out);
  and and_5 (and_5_out, not_6_out, not_7_out, ADRS0);
  and and_6 (and_6_out, not_8_out, ADRS0, not_9_out);
  and and_7 (and_7_out, WSS1, not_10_out, not_11_out);
  and and_8 (and_8_out, WSS1, WSS0, ADRS1, ERRin);
  and and_9 (and_9_out, not_12_out, not_13_out, ADRS0);
  and and_10 (and_10_out, not_14_out, ADRS1, not_15_out);
  and and_11 (and_11_out, not_16_out, ADRS1, not_17_out);
  and and_12 (and_12_out, ADRS1, not_18_out, not_19_out);
  and and_13 (and_13_out, WSS1, not_20_out, ADRS0, not_21_out);
  and and_14 (and_14_out, WSS1, WSS0, not_22_out, not_23_out);
  and and_15 (and_15_out, WSS1, WSS0, ADRS1, ADRS0, ERRin);
  and and_16 (and_16_out, not_24_out, ADRS1, not_25_out);
  and and_17 (and_17_out, not_26_out, ADRS1, not_27_out);
  and and_18 (and_18_out, not_28_out, ADRS1, ADRS0);
  and and_19 (and_19_out, WSS1, WSS0, not_29_out, not_30_out);
  and and_20 (and_20_out, WSS1, WSS0, not_31_out);
  and and_21 (and_21_out, not_32_out, ADRS1, ADRS0, not_33_out);
  and and_22 (and_22_out, WSS1, WSS0, ADRS0, not_34_out);
  and and_23 (and_23_out, WSS1, WSS0, ADRS1, not_35_out);
  and and_24 (and_24_out, not_36_out, ADRS0);
  and and_25 (and_25_out, not_37_out, not_38_out, ADRS1, not_39_out);
  and and_26 (and_26_out, WSS0, ADRS0);
  and and_27 (and_27_out, WSS1, ADRS0);
  and and_28 (and_28_out, not_40_out, not_41_out, ADRS0);
  and and_29 (and_29_out, not_42_out, ADRS0);
  and and_30 (and_30_out, WSS0, ADRS1, not_43_out);
  and and_31 (and_31_out, WSS1, ADRS1, not_44_out);
  or or_1 (B0, and_1_out, and_2_out, and_3_out);
  or or_2 (B1, and_4_out, and_5_out, and_6_out, and_7_out, and_8_out);
  or or_3 (B2, and_9_out, and_10_out, and_11_out, and_12_out, and_13_out, and_14_out, and_15_out);
  or or_4 (B3, and_16_out, and_17_out, and_18_out, and_19_out, and_20_out);
  or or_5 (ERR, and_21_out, and_22_out, and_23_out);
  or or_6 (OrderSel0, and_24_out, and_25_out, and_26_out, and_27_out);
  or or_7 (OrderSel1, and_28_out, and_29_out, and_30_out, and_31_out);
endmodule

module OFCtrl (
  input  [17:0] AdressIn,
  input  ERR,
  output [17:0] AdressOut
);

  wire [17:0] adder_1_out;

  Adder #(.width(18)) adder_1 (.a(AdressIn), .b(18'h1), .out(adder_1_out), .cin(1'b0));  // open: cout
  Multiplexer #(.width(18), .disabled(0), .enable("false")) multiplexer_1 (
    .in0(AdressIn), .in1(adder_1_out), .out(AdressOut), .sel(ERR));
endmodule

module ShiftCtrl (
  input  OrderSel1,
  input  OrderSel0,
  input  B3,
  input  B2,
  input  B1,
  input  B0,
  input  [15:0] UWDout,
  input  [15:0] LWDout,
  input  [7:0] B3Din,
  input  [7:0] B2Din,
  input  [7:0] B1Din,
  input  [7:0] B0Din,
  output [15:0] UWDin,
  output [15:0] LWDin,
  output [7:0] B3Dout,
  output [7:0] B2Dout,
  output [7:0] B1Dout,
  output [7:0] B0Dout,
  output B3F,
  output B2F,
  output B1F,
  output B0F
);

  Shifter #(.width(32), .shift("rl")) shifter_1 (
    .in({UWDout, LWDout}), .\dist ({OrderSel1, OrderSel0, 3'b000}), .out({B3Dout, B2Dout, B1Dout, B0Dout}));
  Shifter #(.width(32), .shift("rl")) shifter_2 (
    .in({B3Din, B2Din, B1Din, B0Din}), .\dist ({OrderSel1, OrderSel0, 3'b000}), .out({UWDin, LWDin}));
  Shifter #(.width(4), .shift("rl")) shifter_3 (
    .in({B3, B2, B1, B0}), .\dist ({OrderSel1, OrderSel0}), .out({B3F, B2F, B1F, B0F}));
endmodule
