// Logisim project RAMInterface.circ as structural Verilog: 2 circuits, main circuit main
module main (
  input  [19:0] Address,
  input  [1:0] WSSel,
  input  WE,
  input  [31:0] DataIn,
  output OPFin,
  output [31:0] DataOut,
  output Busy
);

  wire and_1_out, Clock_out, main_1_b0f, main_1_b1f, main_1_b2f, main_1_b3f, main_1_errorout, not_1_out,
       register_1_q, register_2_q, register_5_q, register_6_q, register_8_q;
  wire [7:0] main_1_b0dout, main_1_b1dout, main_1_b2dout, main_1_b3dout;

  Register #(.width(1)) register_1 (
    .D(main_1_b3f), .en(main_1_b3f), .Q(register_1_q), .clk(and_1_out), .clr(not_1_out));
  Register #(.width(1)) register_2 (
    .D(main_1_b2f), .en(main_1_b2f), .Q(register_2_q), .clk(and_1_out), .clr(not_1_out));
  Register #(.trigger("high")) register_3 (
    .D(main_1_b3dout), .en(main_1_b3f), .Q(DataOut[31:24]), .clk(and_1_out), .clr(not_1_out));
  Register #(.trigger("high")) register_4 (
    .D(main_1_b2dout), .en(main_1_b2f), .Q(DataOut[23:16]), .clk(and_1_out), .clr(not_1_out));
  Register #(.width(1)) register_5 (
    .D(main_1_b0f), .en(main_1_b0f), .Q(register_5_q), .clk(and_1_out), .clr(not_1_out));
  Register #(.width(1)) register_6 (
    .D(main_1_b1f), .en(main_1_b1f), .Q(register_6_q), .clk(and_1_out), .clr(not_1_out));
  Register #(.trigger("high")) register_7 (
    .D(main_1_b1dout), .en(main_1_b1f), .Q(DataOut[15:8]), .clk(and_1_out), .clr(not_1_out));
  Register #(.width(1)) register_8 (.D(main_1_errorout), .en(1'b1), .Q(register_8_q), .clk(and_1_out), .clr(not_1_out));
  Register #(.trigger("high")) register_9 (
    .D(main_1_b0dout), .en(main_1_b0f), .Q(DataOut[7:0]), .clk(and_1_out), .clr(not_1_out));
  ASyncRamSubInt_main main_1 (
    .ErrorIn(register_8_q), .ErrorOut(main_1_errorout), .Address(Address), .WSSel(WSSel), .WE(WE),
    .CE(and_1_out), .B3Dout(main_1_b3dout), .B2Dout(main_1_b2dout), .B1Dout(main_1_b1dout),
    .B0Dout(main_1_b0dout), .B3Din(DataIn[31:24]), .B2Din(DataIn[23:16]), .B1Din(DataIn[15:8]),
    .B0Din(DataIn[7:0]), .B3F(main_1_b3f), .B2F(main_1_b2f), .B1F(main_1_b1f), .B0F(main_1_b0f));
  and and_1 (and_1_out, Clock_out, Busy);
  OPFin opfin_1 (
    .WSSel(WSSel), .B3F(register_1_q), .B2F(register_2_q), .B1F(register_6_q), .B0F(register_5_q),
    .OPFin(OPFin), .AllE(Busy));
  not not_1 (not_1_out, Busy);
  Clock Clock (.out(Clock_out));
endmodule

module OPFin (
  input  [1:0] WSSel,
  input  B3F,
  input  B2F,
  input  B1F,
  input  B0F,
  output AllE,
  output OPFin
);

  wire and_1_out, and_2_out, and_3_out;

  and and_1 (and_1_out, WSSel[1], WSSel[0], B3F, B2F, B1F, B0F);
  and and_2 (and_2_out, WSSel[1], ~WSSel[0], B1F, B0F);  // AND_Gate
  or or_1 (OPFin, and_1_out, and_2_out, and_3_out);
  and and_3 (and_3_out, ~WSSel[1], WSSel[0], B0F);  // AND_Gate
  or or_2 (AllE, WSSel[0], WSSel[1]);
endmodule
