// Logisim project RAMInterfaceOuter.circ as structural Verilog: 3 circuits, main circuit main
module main (
  input  [31:0] DataIn,
  input  [31:0] DataIn_2,
  input  WE,
  input  WE_2,
  input  [1:0] WSSel,
  input  [1:0] WSSel_2,
  input  [19:0] Address,
  input  [19:0] Address_2,
  input  [31:0] DataIn_3,
  input  WE_3,
  input  [1:0] WSSel_3,
  input  [19:0] Address_3,
  output [31:0] DataOut,
  output [31:0] DataOut_2,
  output OPFin,
  output OPFin_2,
  output [31:0] DataOut_3,
  output OPFin_3
);

  wire clock_1_out, main_1_busy, main_1_opfin, not_1_out, or_1_out, or_2_out, or_3_out, plexers_1_we_4;
  wire [1:0] nopsel_1_nop0, plexers_1_wssel_4, register_1_q;
  wire [19:0] plexers_1_address_4;
  wire [31:0] main_1_dataout, plexers_1_datain_4;

  RAMInterface_main main_1 (
    .Busy(main_1_busy), .Address(plexers_1_address_4), .WSSel(plexers_1_wssel_4), .WE(plexers_1_we_4),
    .OPFin(main_1_opfin), .DataIn(plexers_1_datain_4), .DataOut(main_1_dataout));
  not not_1 (not_1_out, main_1_busy);
  Register #(.width(2)) register_1 (
    .D(nopsel_1_nop0), .en(not_1_out), .Q(register_1_q), .clk(clock_1_out));  // open: clr
  NOPSEL nopsel_1 (
    .COP1(register_1_q[1]), .COP0(register_1_q[0]), .REQ3(or_2_out), .REQ2(or_1_out), .REQ1(or_3_out),
    .NOP1(nopsel_1_nop0[1]), .NOP0(nopsel_1_nop0[0]));
  or or_1 (or_1_out, WSSel_3[1], WSSel_3[0]);
  or or_2 (or_2_out, WSSel[1], WSSel[0]);
  or or_3 (or_3_out, WSSel_2[1], WSSel_2[0]);
  Clock clock_1 (.out(clock_1_out));
  Plexers plexers_1 (
    .DataOut_2(DataOut), .DataIn(DataIn), .WE(WE), .WSSel(WSSel), .Address(Address), .OPFin_2(OPFin),
    .Select(register_1_q), .OPFin(main_1_opfin), .DataOut(main_1_dataout), .DataIn_4(plexers_1_datain_4),
    .WE_4(plexers_1_we_4), .WSSel_4(plexers_1_wssel_4), .Address_4(plexers_1_address_4),
    .DataOut_4(DataOut_3), .DataIn_3(DataIn_3), .WE_3(WE_3), .WSSel_3(WSSel_3), .Address_3(Address_3),
    .OPFin_4(OPFin_3), .DataOut_3(DataOut_2), .DataIn_2(DataIn_2), .WE_2(WE_2), .WSSel_2(WSSel_2),
    .Address_2(Address_2), .OPFin_3(OPFin_2));
endmodule

module NOPSEL (
  input  COP1,
  input  COP0,
  input  REQ3,
  input  REQ2,
  input  REQ1,
  output NOP1,
  output NOP0
);

  wire and_1_out, and_2_out, and_3_out, and_4_out, and_5_out, and_6_out, and_7_out, and_8_out, and_9_out,
       and_10_out, not_1_out, not_2_out, not_3_out, not_4_out, not_5_out, not_6_out, not_7_out, not_8_out,
       not_9_out;

  not not_1 (not_1_out, REQ1);
  not not_2 (not_2_out, REQ1);
  not not_3 (not_3_out, COP1);
  not not_4 (not_4_out, COP1);
  not not_5 (not_5_out, COP0);
  not not_6 (not_6_out, COP0);
  not not_7 (not_7_out, REQ2);
  not not_8 (not_8_out, REQ2);
  not not_9 (not_9_out, COP0);
  and and_1 (and_1_out, REQ2, not_1_out);
  and and_2 (and_2_out, REQ3, not_2_out);
  and and_3 (and_3_out, not_3_out, COP0, REQ2);
  and and_4 (and_4_out, not_4_out, COP0, REQ3);
  and and_5 (and_5_out, COP1, not_5_out, REQ3);
  and and_6 (and_6_out, not_6_out, REQ1);
  and and_7 (and_7_out, not_7_out, REQ1);
  and and_8 (and_8_out, REQ3, not_8_out);
  and and_9 (and_9_out, COP1, REQ1);
  and and_10 (and_10_out, COP1, not_9_out, REQ3);
  or or_1 (NOP1, and_1_out, and_2_out, and_3_out, and_4_out, and_5_out);
  or or_2 (NOP0, and_6_out, and_7_out, and_8_out, and_9_out, and_10_out);
endmodule

module Plexers (
  input  [1:0] Select,
  input  OPFin,
  input  [31:0] DataOut,
  input  [31:0] DataIn,
  input  [31:0] DataIn_2,
  input  WE,
  input  WE_2,
  input  [1:0] WSSel,
  input  [1:0] WSSel_2,
  input  [19:0] Address,
  input  [19:0] Address_2,
  input  [31:0] DataIn_3,
  input  WE_3,
  input  [1:0] WSSel_3,
  input  [19:0] Address_3,
  output [31:0] DataIn_4,
  output WE_4,
  output [1:0] WSSel_4,
  output [19:0] Address_4,
  output [31:0] DataOut_2,
  output [31:0] DataOut_3,
  output OPFin_2,
  output [31:0] DataOut_4,
  output OPFin_3,
  output OPFin_4
);

  wire or_1_out;

  Demultiplexer #(.select(2), .disabled(0)) demultiplexer_1 (
    .out1(OPFin_3), .out2(OPFin_4), .out3(OPFin_2), .in(OPFin), .sel(Select), .en(or_1_out));  // open: out0
  or or_1 (or_1_out, Select[0], Select[1]);
  Multiplexer #(.select(2), .width(32), .disabled(0)) multiplexer_1 (
    .in1(DataIn_2), .in2(DataIn_3), .in3(DataIn), .out(DataIn_4), .sel(Select), .en(or_1_out));  // open: in0
  Multiplexer #(.select(2), .disabled(0)) multiplexer_2 (
    .in1(WE_2), .in2(WE_3), .in3(WE), .out(WE_4), .sel(Select), .en(or_1_out));  // open: in0
  Multiplexer #(.select(2), .width(2), .disabled(0)) multiplexer_3 (
    .in1(WSSel_2), .in2(WSSel_3), .in3(WSSel), .out(WSSel_4), .sel(Select), .en(or_1_out));  // open: in0
  Multiplexer #(.select(2), .width(20), .disabled(0)) multiplexer_4 (
    .in1(Address_2), .in2(Address_3), .in3(Address), .out(Address_4), .sel(Select), .en(or_1_out));  // open: in0

  assign DataOut_2 = DataOut;
  assign DataOut_3 = DataOut;
  assign DataOut_4 = DataOut;
endmodule
