// Logisim project UnitSRAM simulator.circ as structural Verilog: 2 circuits, main circuit main
module main (
  input  [17:0] Address,
  input  CE,
  input  UB,
  input  LB,
  input  WE,
  input  OE,
  input  [15:0] Din,
  output [15:0] Dout
);

  wire not_1_out, not_2_out, ram_sim_control_1_ld, ram_sim_control_1_sel1, ram_sim_control_1_sel2;
  wire [15:0] ram_1_data;

  not not_1 (not_1_out, CE);
  ram_sim_control ram_sim_control_1 (
    .CE(not_1_out), .UB(UB), .LB(LB), .WE(WE), .OE(OE), .sel1(ram_sim_control_1_sel1),
    .sel2(ram_sim_control_1_sel2), .ld(ram_sim_control_1_ld));
  assign Dout = ram_sim_control_1_ld ? ram_1_data : 16'bz;  // Controlled_Buffer controlled_buffer_1
  RAM #(.addrWidth(18), .bus("asynch")) ram_1 (
    .addr(Address), .data(ram_1_data[7:0]), .sel(ram_sim_control_1_sel2), .ld(ram_sim_control_1_ld));  // open: clr
  assign ram_1_data = not_2_out ? Din : 16'bz;  // Controlled_Buffer controlled_buffer_2
  not not_2 (not_2_out, ram_sim_control_1_ld);
  RAM #(.addrWidth(18), .bus("asynch")) ram_2 (
    .addr(Address), .data(ram_1_data[15:8]), .sel(ram_sim_control_1_sel1), .ld(ram_sim_control_1_ld));  // open: clr
endmodule

module ram_sim_control (
  input  CE,
  input  UB,
  input  LB,
  input  WE,
  input  OE,
  output sel1,
  output sel2,
  output ld
);

  wire and_1_out, and_2_out, and_3_out, and_4_out, not_1_out, not_2_out, not_3_out, not_4_out;

  not not_1 (not_1_out, WE);
  not not_2 (not_2_out, OE);
  not not_3 (not_3_out, WE);
  not not_4 (not_4_out, OE);
  and and_1 (and_1_out, CE, UB, not_1_out, OE);
  and and_2 (and_2_out, CE, UB, WE, not_2_out);
  and and_3 (and_3_out, CE, LB, not_3_out, OE);
  and and_4 (and_4_out, CE, LB, WE, not_4_out);
  or or_1 (sel1, and_1_out, and_2_out);
  or or_2 (sel2, and_3_out, and_4_out);

  assign ld = OE;
endmodule
