// Logisim project ClockSpeeds.circ as structural Verilog: 1 circuit, main circuit main
module main (
  input  in_1,
  output out_2
);

  wire clock_1_out, comparator_2_eq, not_1_out, or_1_out, register_1_q;
  wire [3:0] counter_1_q;

  Clock clock_1 (.out(clock_1_out));
  or or_1 (or_1_out, clock_1_out, in_1);
  not not_1 (not_1_out, register_1_q);
  Counter #(.width(4), .max('hf)) counter_1 (
    .Q(counter_1_q), .clk(clock_1_out), .clr(comparator_2_eq));  // open: load, D, count, carry
  Register #(.width(1)) register_1 (.D(not_1_out), .en(1'b1), .Q(register_1_q), .clk(or_1_out), .clr(1'b0));
  Comparator #(.width(4)) comparator_1 (.a(4'b0000), .b(counter_1_q), .eq(out_2));  // open: gt, lt
  Comparator #(.width(4)) comparator_2 (.a(4'b0011), .b(counter_1_q), .eq(comparator_2_eq));  // open: gt, lt
endmodule
