// Logisim project successful-1 - project 205.circ as structural Verilog: 1 circuit, main circuit main
module main (
  input  [7:0] in_1,
  input  [7:0] in_2,
  input  in_3,
  input  [1:0] in_4,
  output [7:0] out_5
);

  wire adder_1_cout, and_2_out, clock_1_out, undriven;
  wire [7:0] adder_1_out, and_1_out, RDST_q, RSRC_q;

  Register RDST (.D(in_1), .en(1'b1), .Q(RDST_q), .clk(clock_1_out));  // open: clr
  Clock clock_1 (.out(clock_1_out));
  Register RSRC (.D(in_2), .en(1'b1), .Q(RSRC_q), .clk(clock_1_out));  // open: clr
  Adder adder_1 (.a(RSRC_q), .b(RDST_q), .out(adder_1_out), .cin(undriven), .cout(adder_1_cout));
  assign and_1_out = RSRC_q & RDST_q;  // AND_Gate and_1, 8 bits wide
  buf xor_1 (in_3, undriven);  // XOR_Gate
  Multiplexer #(.select(2), .width(8), .enable("false")) multiplexer_1 (
    .in0(adder_1_out), .in1(and_1_out), .in3(RSRC_q), .out(out_5), .sel(in_4));  // open: in2
  and and_2 (and_2_out, in_4[0], in_4[1]);
  assign in_1 = and_2_out ? out_5 : 8'bz;  // Controlled_Buffer controlled_buffer_1
endmodule
