// Logisim project Bus.circ as structural Verilog: 1 circuit, main circuit main
module main (
  input  in_1,
  input  [7:0] in_2,
  input  in_3,
  input  in_4,
  input  in_5,
  input  in_6,
  input  in_7,
  input  in_8,
  input  in_9,
  input  in_10,
  input  in_11,
  input  in_12,
  input  in_13,
  input  in_14,
  input  in_15,
  output [7:0] out_16
);

  wire clock_1_out;
  wire [7:0] adder_1_out, controlled_buffer_7_out, R1_q, R2_q, R3_q, R4_q, Y_2_q, Y_q;

  Clock clock_1 (.out(clock_1_out));
  Register R1 (.D(out_16), .en(in_3), .Q(R1_q), .clk(clock_1_out));  // open: clr
  Register R2 (.D(out_16), .en(in_5), .Q(R2_q), .clk(clock_1_out));  // open: clr
  Register R3 (.D(out_16), .en(in_7), .Q(R3_q), .clk(clock_1_out));  // open: clr
  Register R4 (.D(out_16), .en(in_10), .Q(R4_q), .clk(clock_1_out));  // open: clr
  Register Y (.D(out_16), .en(in_14), .Q(Y_q), .clk(clock_1_out));  // open: clr
  assign out_16 = in_1 ? in_2 : 8'bz;  // Controlled_Buffer controlled_buffer_1
  assign out_16 = in_4 ? R1_q : 8'bz;  // Controlled_Buffer controlled_buffer_2
  assign out_16 = in_6 ? R2_q : 8'bz;  // Controlled_Buffer controlled_buffer_3
  assign out_16 = in_8 ? R3_q : 8'bz;  // Controlled_Buffer controlled_buffer_4
  assign out_16 = in_11 ? R4_q : 8'bz;  // Controlled_Buffer controlled_buffer_5
  assign out_16 = in_15 ? Y_q : 8'bz;  // Controlled_Buffer controlled_buffer_6
  assign controlled_buffer_7_out = in_12 ? out_16 : 8'bz;  // Controlled_Buffer controlled_buffer_7
  assign out_16 = in_9 ? Y_2_q : 8'bz;  // Controlled_Buffer controlled_buffer_8
  Adder adder_1 (.a(controlled_buffer_7_out), .b(Y_q), .out(adder_1_out));  // open: cin, cout
  Register Y_2 (.D(adder_1_out), .en(in_13), .Q(Y_2_q), .clk(clock_1_out));  // open: clr
endmodule
