// Logisim project CU.circ as structural Verilog: 1 circuit, main circuit main
module main (
  input  [15:0] IPout,
  input  CLK,
  output [3:0] out_3,
  output [3:0] out_4,
  output out_5,
  output out_6,
  output [3:0] out_7,
  output [3:0] out_8,
  output [3:0] out_9,
  output out_10
);

  wire and_1_out, not_1_out;
  wire [3:0] counter_1_q;
  wire [15:0] rom_1_data, rom_2_data;

  ROM #(.addrWidth(16), .dataWidth(16)) rom_1 (
    .addr(IPout), .data({rom_1_data[15], out_3, rom_1_data[10:8], out_4[3:2], rom_1_data[5:0]}));  // open: sel
  not not_1 (not_1_out, and_1_out);
  Counter #(.width(4), .max('hf)) counter_1 (
    .load(and_1_out), .D(4'b0000), .count(not_1_out), .Q(counter_1_q), .clk(CLK));  // open: carry, clr
  and and_1 (and_1_out, rom_2_data[15], rom_2_data[14], rom_2_data[13], rom_2_data[12]);
  ROM #(.addrWidth(9), .dataWidth(16)) rom_2 (
    .addr({rom_1_data[15], out_3, counter_1_q}), .data(rom_2_data));  // open: sel
  // CUsel_main main_1: pin names not known; wires that end beside it: rom_2_data, out_7, out_10, {out_4[3:2], 2'b00}, out_8, {2'b00, rom_1_data[10:9]}, out_3, out_9, out_6, out_5

  assign out_4[1:0] = 2'b00;

  // Notes on the sheet:
  //   contents of rom_1 (hex, n*v repeats v):
  //   4*40
  //   contents of rom_2 (hex, n*v repeats v):
  //   9040 2050 b500 8752 f572 ffff 10*0 9040 2050 b500 8752 f572 ffff 10*0 9040 2050 b500 8752 f572 ffff
  //   10*0 9040 2050 b500 8752 f572 ffff 10*0 9040 2050 b500 8752 f572 ffff 10*0 9040 2050 b500 8752 f572
  //   ffff 10*0 9040 2050 b500 8752 f572 ffff 10*0 9040 2050 b500 8752 f572 ffff 10*0 9040 2050 b500 8752
  //   f572 ffff 10*0 9040 2050 b500 8752 f572 ffff 10*0 9040 2050 b500 8752 f572 ffff 10*0 9040 2050 b500
  //   8752 f572 ffff 10*0 9040 2050 b500 8752 f572 ffff 10*0 9040 2050 b500 8752 f572 ffff 10*0 9040 2050
  //   b500 8752 f572 ffff 10*0 9040 2050 b500 8752 f572 ffff 12*0 b500
endmodule
