// Logisim project PROtry1.circ as structural Verilog: 1 circuit, main circuit main
module main (
);

  wire [7:0] adder_1_out, and_1_out, multiplexer_1_out, RDST_q, RSRC_q;

  Register RDST (.Q(RDST_q));  // open: D, en, clk, clr
  Register RSRC (.Q(RSRC_q));  // open: D, en, clk, clr
  Adder adder_1 (.a(RSRC_q), .b(RDST_q), .out(adder_1_out));  // open: cin, cout
  assign and_1_out = RSRC_q & RDST_q;  // AND_Gate and_1, 8 bits wide
  Multiplexer #(.select(2), .width(8), .enable("false")) multiplexer_1 (
    .in0(adder_1_out), .in1(and_1_out), .out(multiplexer_1_out));  // open: in2, in3, sel
  Register register_1 (.D(multiplexer_1_out), .en(1'b1));  // open: Q, clk, clr
endmodule
