// Logisim project TOP.circ as structural Verilog: 1 circuit, main circuit main
module main (
);

  wire clock_1_out, main_1_ivre, main_1_sele, main_1_zfe, main_1_zfe_2, main_2_cfout, main_2_zfout;
  wire [3:0] main_1_out_11, main_1_readse, main_1_writesel;
  wire [8:0] main_1_romad;
  wire [15:0] main_1_ivout, rom_1_data;
  wire [23:0] main_2_irout;

  Clock clock_1 (.out(clock_1_out));
  ROM #(.addrWidth(9), .dataWidth(16)) rom_1 (.addr(main_1_romad), .data(rom_1_data));  // open: sel
  CUsel_main main_1 (
    .ROMin(rom_1_data), .READse(main_1_readse), .WRITEsel(main_1_writesel), .out_11(main_1_out_11),
    .ZFe(main_1_zfe), .ZFe_2(main_1_zfe_2), .CLK(clock_1_out), .SELe(main_1_sele), .ROMad(main_1_romad),
    .IRin(main_2_irout), .IVout(main_1_ivout), .IVre(main_1_ivre), .ZFin(main_2_zfout), .CFin(main_2_cfout));  // open: SELe_2
  BUSnew_main main_2 (
    .IRout(main_2_irout), .CLK(clock_1_out), .SELe(main_1_sele), .WRITEsel(main_1_writesel),
    .ALUsel(main_1_out_11), .READsel(main_1_readse), .CFe(main_1_zfe_2), .ZFe(main_1_zfe),
    .IVrin(main_1_ivre), .IVin(main_1_ivout), .CFout(main_2_cfout), .ZFout(main_2_zfout));  // open: IPae, IPae_2, DATAout

  // Notes on the sheet:
  //   contents of rom_1 (hex, n*v repeats v):
  //   8ab0 8ab0 9040 2050 b500 8752 8572 ffff 8*0 8ab0 8ab0 9040 2050 b500 8752 8572 ffff 8*0 8ab0 8ab0
  //   2050 b500 8752 8572 ffff 9*0 8ab0 8ab0 2050 b500 8752 8572 ffff 9*0 8ab0 8ab0 9040 2050 b500 8752
  //   8572 ffff 8*0 8ab0 8ab0 9040 2050 b500 8752 8572 ffff 8*0 8ab0 8ab0 9040 2050 b500 8752 8572 ffff
  //   8*0 8ab0 8ab0 9040 2050 b500 8752 8572 ffff 8*0 8ab0 8ab0 9040 2050 b500 8752 8572 ffff 8*0 8ab0
  //   8ab0 9040 2050 b500 8752 8572 ffff 8*0 8ab0 8ab0 9040 2050 b500 8752 8572 ffff 8*0 8ab0 8ab0 9040
  //   2050 b500 8752 8572 ffff 8*0 8ab0 8ab0 9040 2050 b500 8752 8572 ffff 8*0 8ab0 8ab0 9040 2050 b500
  //   8752 8572 ffff 8*0 8ab0 8ab0 9040 2050 b500 8752 8572 ffff 8*0 8ab0 8ab0 9040 2050 b500 8752 8572
  //   ffff 8*0 8ab0 8ab0 c000 8752 8572 ffff 10*0 8ab0 8ab0 a040 c000 d400 8752 8572 ffff 8*0 8ab0 8ab0
  //   9040 8750 8572 ffff 10*0 8ab0 8ab0 9040 a051 8752 8572 ffff 9*0 8ab0 8ab0 9060 8f90 b900 8752 8572
  //   ffff 8*0 8ab0 8ab0 9060 a0a0 8752 8572 ffff 9*0 8ab0 8ab0 9060 a051 a0a0 b900 8752 8572 ffff 7*0
  //   8ab0 8ab0 9040 8750 8572 ffff 10*0 8ab0 8ab0 9040 8750 8572 ffff 10*0 8ab0 8ab0 9040 8750 8572 ffff
  //   10*0 8ab0 8ab0 253 8520 9040 8750 8572 ffff 8*0 8ab0 8ab0 8c60 a0a0 8c53 85c0 8752 8572 ffff 7*0
  //   8ab0 8ab0 8c52 85c0 8c60 8f90 b900 8752 8572 ffff 6*0 8ab0 8ab0 8c60 87a0 9070 8c53 85c0 ffff 8*0
  //   8ab0 8ab0 8c52 85c0 8c60 8f90 8970 8752 8572 ffff
endmodule
